// Logisim project LOGIC GATE.circ as structural Verilog: 1 circuit, main circuit main
module main (
  input  A,
  input  B,
  input  B_2,
  input  A_2,
  input  C,
  output Difference,
  output borrow,
  output out_8,
  output BORROW_2
);

  wire and_1_out, and_3_out, not_1_out, not_2_out, not_3_out, xor_1_out;

  not not_1 (not_1_out, A_2);
  not not_2 (not_2_out, A);
  xor xor_1 (xor_1_out, A_2, C);
  and and_1 (and_1_out, C, not_1_out);
  xor xor_2 (Difference, A, B);
  and and_2 (borrow, B, not_2_out);
  xor xor_3 (out_8, B_2, xor_1_out);
  not not_3 (not_3_out, xor_1_out);
  and and_3 (and_3_out, not_3_out, B_2);
  or or_1 (BORROW_2, and_3_out, and_1_out);

  // Notes on the sheet:
  //   half subtractor
  //   full subtracter
  //   DIFFERENCE 
endmodule
